// Logisim project cpu.circ as structural Verilog: 4 circuits, main circuit main
module main (
  input  [31:0] INSTRUCTION,
  input  CLOCK,
  output [31:0] ra,
  output [31:0] sp,
  output [31:0] t0,
  output [31:0] t1,
  output [31:0] t2,
  output [31:0] s0,
  output [31:0] s1,
  output [31:0] a0,
  output [31:0] FETCH_ADDRESS
);

  wire branchcomp_1_breq, branchcomp_1_brlt, controllogic_1_asel, controllogic_1_brun, controllogic_1_bsel,
       controllogic_1_immsel, controllogic_1_memrw, controllogic_1_regwen, controllogic_1_wbsel;
  wire [3:0] controllogic_1_alusel;
  wire [31:0] adder_1_out, Arithmetic_Logic_Unit_result, DMEM_p5, immgen_1_immgen031, multiplexer_1_out,
       multiplexer_2_out, multiplexer_3_out, RegFile_read_data_1, RegFile_read_data_2;

  Adder #(.width(32)) adder_1 (.a(FETCH_ADDRESS), .b(32'h1), .out(adder_1_out));  // open: cin, cout
  Register #(.width(32)) PC (.D(adder_1_out), .clk(CLOCK), .Q(FETCH_ADDRESS));  // open: en, clr
  Controllogic controllogic_1 (
    .INSTRUCTION(INSTRUCTION), .BrEq(branchcomp_1_breq), .BrLT(branchcomp_1_brlt),
    .RegWEn(controllogic_1_regwen), .ALUSel(controllogic_1_alusel), .MemRW(controllogic_1_memrw),
    .BSel(controllogic_1_bsel), .WBSel(controllogic_1_wbsel), .ASel(controllogic_1_asel),
    .ImmSel(controllogic_1_immsel), .BrUn(controllogic_1_brun));
  regfile_main RegFile (
    .rs2(INSTRUCTION[24:20]), .rd(INSTRUCTION[11:7]), .Read_Data_1(RegFile_read_data_1),
    .Read_Data_2(RegFile_read_data_2), .ra(ra), .sp(sp), .t0(t0), .t1(t1), .t2(t2), .s0(s0), .s1(s1),
    .a0(a0), .rs1(INSTRUCTION[19:15]), .Write_Data(multiplexer_3_out), .RegWEn(controllogic_1_regwen),
    .clk(CLOCK));
  ImmGen immgen_1 (.ImmSel(controllogic_1_immsel), .Instruction(INSTRUCTION), .ImmGen031(immgen_1_immgen031));
  BranchComp branchcomp_1 (
    .DataA(RegFile_read_data_1), .DataB(RegFile_read_data_2), .BrUn(controllogic_1_brun),
    .BrEq(branchcomp_1_breq), .BrLT(branchcomp_1_brlt));
  Multiplexer #(.width(32), .enable("false")) multiplexer_1 (
    .in0(RegFile_read_data_1), .out(multiplexer_1_out), .sel(controllogic_1_asel));  // open: in1
  Multiplexer #(.width(32), .enable("false")) multiplexer_2 (
    .in0(RegFile_read_data_2), .in1(immgen_1_immgen031), .out(multiplexer_2_out), .sel(controllogic_1_bsel));
  alu Arithmetic_Logic_Unit (
    .A(multiplexer_1_out), .B(multiplexer_2_out), .ALUSel(controllogic_1_alusel),
    .Result(Arithmetic_Logic_Unit_result));
  // mem_main DMEM: pin names not known; wires that end beside it: Arithmetic_Logic_Unit_result, RegFile_read_data_2, controllogic_1_memrw, CLOCK, DMEM_p5
  Multiplexer #(.width(32), .enable("false")) multiplexer_3 (
    .in0(Arithmetic_Logic_Unit_result), .in1(DMEM_p5), .out(multiplexer_3_out), .sel(controllogic_1_wbsel));

  // Other names for the same wires on the sheet: clk = CLOCK; fetch_addr[31:0] = FETCH_ADDRESS;
  //   rd[4:0] = INSTRUCTION[11:7]; rs1[4:0] = INSTRUCTION[19:15]; rs2[4:0] = INSTRUCTION[24:20]

  // Notes on the sheet:
  //   Output
  //   Inputs/Outputs from run.circ. DO NOT MOVE THESE.
  //   Inputs
  //   Inputs/Outputs from run.circ. DO NOT MOVE THESE.
endmodule

module Controllogic (
  input  [31:0] INSTRUCTION,
  input  BrEq,
  input  BrLT,
  output RegWEn,
  output [3:0] ALUSel,
  output MemRW,
  output BSel,
  output WBSel,
  output ASel,
  output ImmSel,
  output BrUn
);

  wire add, addi, and1, and_1_out, and_2_out, and_3_out, and_4_out, and_5_out, and_6_out, and_7_out,
       and_8_out, and_22_out, and_23_out, andi, beq, blt, bltu, bne, comparator_1_eq, comparator_2_eq,
       comparator_3_eq, comparator_4_eq, comparator_5_eq, comparator_6_eq, comparator_7_eq, comparator_8_eq,
       comparator_9_eq, comparator_10_eq, comparator_11_eq, comparator_12_eq, comparator_13_eq,
       comparator_14_eq, comparator_15_eq, comparator_16_eq, comparator_17_eq, comparator_18_eq,
       comparator_19_eq, comparator_20_eq, comparator_21_eq, comparator_22_eq, comparator_23_eq,
       comparator_24_eq, comparator_25_eq, comparator_26_eq, comparator_27_eq, comparator_28_eq,
       comparator_29_eq, comparator_30_eq, comparator_31_eq, divu, jal, jalr, lb, lh, lui, lw, mul, mulh,
       mulhu, or1, ori, remu, sll1, slli, slt, slti, srai, srl1, srli, sub, sw, xor1, xori;

  Comparator #(.width(7)) comparator_1 (.a(INSTRUCTION[6:0]), .b(7'b0110011), .eq(comparator_1_eq));  // open: gt, lt
  Comparator #(.width(3)) comparator_2 (.a(INSTRUCTION[14:12]), .b(3'b000), .eq(comparator_2_eq));  // open: gt, lt
  Comparator #(.width(3)) comparator_3 (.a(INSTRUCTION[14:12]), .b(3'b001), .eq(comparator_3_eq));  // open: gt, lt
  Comparator #(.width(3)) comparator_4 (.a(INSTRUCTION[14:12]), .b(3'b010), .eq(comparator_4_eq));  // open: gt, lt
  Comparator #(.width(3)) comparator_5 (.a(INSTRUCTION[14:12]), .b(3'b011), .eq(comparator_5_eq));  // open: gt, lt
  Comparator #(.width(3)) comparator_6 (.a(INSTRUCTION[14:12]), .b(3'b100), .eq(comparator_6_eq));  // open: gt, lt
  Comparator #(.width(3)) comparator_7 (.a(INSTRUCTION[14:12]), .b(3'b101), .eq(comparator_7_eq));  // open: gt, lt
  Comparator #(.width(3)) comparator_8 (.a(INSTRUCTION[14:12]), .b(3'b110), .eq(comparator_8_eq));  // open: gt, lt
  Comparator #(.width(3)) comparator_9 (.a(INSTRUCTION[14:12]), .b(3'b111), .eq(comparator_9_eq));  // open: gt, lt
  and and_1 (and_1_out, comparator_1_eq, comparator_3_eq);
  and and_2 (and_2_out, comparator_1_eq, comparator_4_eq);
  and and_3 (and_3_out, comparator_1_eq, comparator_5_eq);
  and and_4 (and_4_out, comparator_1_eq, comparator_6_eq);
  and and_5 (and_5_out, comparator_1_eq, comparator_7_eq);
  and and_6 (and_6_out, comparator_1_eq, comparator_8_eq);
  and and_7 (and_7_out, comparator_1_eq, comparator_9_eq);
  and and_8 (and_8_out, comparator_1_eq, comparator_2_eq);
  Comparator #(.width(7)) comparator_10 (.a(INSTRUCTION[31:25]), .b({7{1'b0}}), .eq(comparator_10_eq));  // open: gt, lt
  Comparator #(.width(7)) comparator_11 (
    .a(INSTRUCTION[31:25]), .b(7'b0000001), .eq(comparator_11_eq));  // open: gt, lt
  Comparator #(.width(7)) comparator_12 (
    .a(INSTRUCTION[31:25]), .b(7'b0100000), .eq(comparator_12_eq));  // open: gt, lt
  and and_9 (add, and_8_out, comparator_10_eq);
  and and_10 (mul, and_8_out, comparator_11_eq);
  and and_11 (sub, and_8_out, comparator_12_eq);
  and and_12 (sll1, and_1_out, comparator_10_eq);
  and and_13 (mulh, and_1_out, comparator_11_eq);
  and and_14 (slt, comparator_10_eq, and_2_out);
  and and_15 (mulhu, comparator_11_eq, and_3_out);
  and and_16 (xor1, comparator_10_eq, and_4_out);
  and and_17 (divu, comparator_11_eq, and_5_out);
  and and_18 (srl1, comparator_10_eq, and_5_out);
  and and_19 (or1, comparator_10_eq, and_6_out);
  and and_20 (remu, comparator_11_eq, and_7_out);
  and and_21 (and1, comparator_10_eq, and_7_out);
  Comparator #(.width(7)) comparator_13 (.a(INSTRUCTION[6:0]), .b(7'b0000011), .eq(comparator_13_eq));  // open: gt, lt
  Comparator #(.width(7)) comparator_14 (.a(INSTRUCTION[6:0]), .b(7'b0010011), .eq(comparator_14_eq));  // open: gt, lt
  Comparator #(.width(3)) comparator_15 (.a(INSTRUCTION[14:12]), .b(3'b000), .eq(comparator_15_eq));  // open: gt, lt
  Comparator #(.width(3)) comparator_16 (.a(INSTRUCTION[14:12]), .b(3'b001), .eq(comparator_16_eq));  // open: gt, lt
  Comparator #(.width(3)) comparator_17 (.a(INSTRUCTION[14:12]), .b(3'b010), .eq(comparator_17_eq));  // open: gt, lt
  Comparator #(.width(3)) comparator_18 (.a(INSTRUCTION[14:12]), .b(3'b100), .eq(comparator_18_eq));  // open: gt, lt
  Comparator #(.width(3)) comparator_19 (.a(INSTRUCTION[14:12]), .b(3'b101), .eq(comparator_19_eq));  // open: gt, lt
  Comparator #(.width(3)) comparator_20 (.a(INSTRUCTION[14:12]), .b(3'b110), .eq(comparator_20_eq));  // open: gt, lt
  Comparator #(.width(3)) comparator_21 (.a(INSTRUCTION[14:12]), .b(3'b111), .eq(comparator_21_eq));  // open: gt, lt
  Comparator #(.width(7)) comparator_22 (.a(INSTRUCTION[31:25]), .b({7{1'b0}}), .eq(comparator_22_eq));  // open: gt, lt
  Comparator #(.width(7)) comparator_23 (
    .a(INSTRUCTION[31:25]), .b(7'b0100000), .eq(comparator_23_eq));  // open: gt, lt
  Comparator #(.width(7)) comparator_24 (.a(INSTRUCTION[6:0]), .b(7'b1100111), .eq(comparator_24_eq));  // open: gt, lt
  and and_22 (and_22_out, comparator_14_eq, comparator_16_eq);
  and and_23 (and_23_out, comparator_14_eq, comparator_19_eq);
  and and_24 (lb, comparator_13_eq, comparator_15_eq);
  and and_25 (lh, comparator_13_eq, comparator_16_eq);
  and and_26 (lw, comparator_13_eq, comparator_17_eq);
  and and_27 (addi, comparator_14_eq, comparator_15_eq);
  and and_28 (slli, and_22_out, comparator_22_eq);
  and and_29 (slti, comparator_14_eq, comparator_17_eq);
  and and_30 (xori, comparator_14_eq, comparator_18_eq);
  and and_31 (srli, and_23_out, comparator_22_eq);
  and and_32 (srai, and_23_out, comparator_23_eq);
  and and_33 (ori, comparator_14_eq, comparator_20_eq);
  and and_34 (andi, comparator_14_eq, comparator_21_eq);
  and and_35 (jalr, comparator_15_eq, comparator_24_eq);
  Comparator #(.width(7)) comparator_25 (.a(INSTRUCTION[6:0]), .b(7'b0100011), .eq(comparator_25_eq));  // open: gt, lt
  Comparator #(.width(3)) comparator_26 (.a(INSTRUCTION[14:12]), .b(3'b010), .eq(comparator_26_eq));  // open: gt, lt
  Comparator #(.width(7)) comparator_27 (.a(INSTRUCTION[6:0]), .b(7'b1100011), .eq(comparator_27_eq));  // open: gt, lt
  Comparator #(.width(3)) comparator_28 (.a(INSTRUCTION[14:12]), .b(3'b000), .eq(comparator_28_eq));  // open: gt, lt
  Comparator #(.width(3)) comparator_29 (.a(INSTRUCTION[14:12]), .b(3'b100), .eq(comparator_29_eq));  // open: gt, lt
  Comparator #(.width(3)) comparator_30 (.a(INSTRUCTION[14:12]), .b(3'b110), .eq(comparator_30_eq));  // open: gt, lt
  Comparator #(.width(3)) comparator_31 (.a(INSTRUCTION[14:12]), .b(3'b001), .eq(comparator_31_eq));  // open: gt, lt
  Comparator #(.width(7)) comparator_32 (.a(INSTRUCTION[6:0]), .b(7'b0110111), .eq(lui));  // open: gt, lt
  Comparator #(.width(7)) comparator_33 (.a(INSTRUCTION[6:0]), .b(7'b1101111), .eq(jal));  // open: gt, lt
  and and_36 (sw, comparator_25_eq, comparator_26_eq);
  and and_37 (beq, comparator_27_eq, comparator_28_eq);
  and and_38 (blt, comparator_27_eq, comparator_29_eq);
  and and_39 (bltu, comparator_27_eq, comparator_30_eq);
  and and_40 (bne, comparator_27_eq, comparator_31_eq);

  // Other names for the same wires on the sheet: Opcode[6:0] = INSTRUCTION[6:0]; funct3[2:0] = INSTRUCTION[14:12];
  //   funct7[6:0] = INSTRUCTION[31:25]

  // Notes on the sheet:
  //   R-type Instructions
  //   compare opcode
  //   compare funct3
  //   compare funct7
  //   compare opcode
  //   compare funct3
  //   compare funct7
  //   I-type Instructions
  //   compare opcode
  //   compare funct3
  //   compare opcode
  //   compare funct3
  //   compare opcode
  //   compare opcode
  //   S-type Instruction
  //   SB-type Instructions
  //   U-type Instruction
  //   UJ-type Instruction
endmodule

module ImmGen (
  input  ImmSel,
  input  [31:0] Instruction,
  output [31:0] ImmGen031
);

  wire [31:11] I_Format, S_Format;
  wire [31:12] B_Format;
  wire [31:20] J_Format;

  assign I_Format = {{20{Instruction[31]}}, Instruction[31]};  // Bit_Extender bit_extender_1
  assign S_Format = {{20{Instruction[31]}}, Instruction[31]};  // Bit_Extender bit_extender_2
  assign B_Format = {{19{Instruction[31]}}, Instruction[31]};  // Bit_Extender bit_extender_3
  assign J_Format = {{11{Instruction[31]}}, Instruction[31]};  // Bit_Extender bit_extender_4

  // Other names for the same wires on the sheet: B_Format[11:1] = {Instruction[7], Instruction[30:25], Instruction[11:8]};
  //   S_Format[10:0] = {Instruction[30:25], Instruction[11:7]}; Imm_out[31:0] = ImmGen031;
  //   I_Format[10:0] = Instruction[30:20]; J_Format[19:1] = {Instruction[19:12], Instruction[20], Instruction[30:21]};
  //   U_Format[31:12] = Instruction[31:12]
endmodule

module BranchComp (
  input  [31:0] DataA,
  input  [31:0] DataB,
  input  BrUn,
  output BrEq,
  output BrLT
);

  wire comparator_1_eq, comparator_1_lt, comparator_2_eq, comparator_2_lt;

  Comparator #(.width(32)) comparator_1 (.a(DataA), .b(DataB), .eq(comparator_1_eq), .lt(comparator_1_lt));  // open: gt
  Comparator #(.width(32), .mode("unsigned")) comparator_2 (
    .a(DataA), .b(DataB), .eq(comparator_2_eq), .lt(comparator_2_lt));  // open: gt
  Multiplexer #(.enable("false")) multiplexer_1 (.in0(comparator_1_eq), .in1(comparator_2_eq), .out(BrEq), .sel(BrUn));
  Multiplexer #(.enable("false")) multiplexer_2 (.in0(comparator_1_lt), .in1(comparator_2_lt), .out(BrLT), .sel(BrUn));

  // Other names for the same wires on the sheet: A[31:0] = DataA; B[31:0] = DataB
endmodule
